# Fritzing sketch Adaptive Diagnosis System (saved by Fritzing 1.0.8)
breadboards: 1

parts:
  STM32 = STM32 Nucleo boards
  INA219_-_MOTOR = INA219
  INA219_-_Circuit = INA219
  DS1 = DS18B20 1-Wire Temperature Sensor Probe Cable
  4_7k_pull-up = Resistor [tolerance=±5% power=0.25W resistance=4.7k package=THT]
  Power_Supply = DC Power Supply [voltage=12V internal_resistance=1Ω max_current=5A]
  Motor_Driver_-_Cytron_MD10C = MD10C R2
  12V_DC_Motor = DC Motor [voltage_(max)=12V voltage_(min)=3V]
  Main_Fuse = Fuse with Handler [part_number=Htc-15m]
  Kill_Switch = SWITCH-SPST-2 [package=switch-spst-vertical]
  Switch_Relay = 2RelayModule
  Power_distribution = PDP
  Motor_Fuse = Fuse with Handler [part_number=Htc-15m]
  Circuit_Fuse = Fuse with Handler [part_number=Htc-15m]
  J1 = XL4015 DC-DC CC CV module (blue)
  V-Probe = BANANA_CONN [package=banana_conn]
  COM = BANANA_CONN [package=banana_conn]
  R1 = Resistor [tolerance=±5% resistance=30k package="2512 [SMD]"]
  R2 = Resistor [tolerance=±5% resistance=10k package="2512 [SMD]"]
  C2 = Electrolytic Capacitor [capacitance=100nF voltage=35V package="1010 [SMD, electrolytic]"]
  Positive_Clamp = BAT54S Dual Schottky Clamp
  Negative_Clamp = BAT54S Dual Schottky Clamp
  ExCircuit_+ = BANANA_CONN [package=banana_conn]
  ExCircuit_- = BANANA_CONN [package=banana_conn]
  A1 = Raspberry Pi 5  # not connected

nets:
  N1: STM32.A0, R1.Pin_0, R2.Pin_1, C2.+, Positive_Clamp.Pin_1_A1, Negative_Clamp.Pin_3_K1/A2
  N2: STM32.A4/SDA, INA219_-_MOTOR.SDA, INA219_-_Circuit.SDA
  N3: STM32.A5/SCL, INA219_-_MOTOR.SCL, INA219_-_Circuit.SCL
  N4: STM32.D2, DS1.DQ, 4_7k_pull-up.Pin_0
  N5: STM32.D4, Switch_Relay.IN1
  N6: STM32.D5_PWM, Switch_Relay.IN2
  N7: STM32.D6_PWM, Motor_Driver_-_Cytron_MD10C.no_name_yet#connector_2
  N8: STM32.D7, Motor_Driver_-_Cytron_MD10C.no_name_yet#connector_1
  VCC: STM32.3V3, INA219_-_MOTOR.VCC, INA219_-_Circuit.VCC, DS1.VDD, 4_7k_pull-up.Pin_1, Positive_Clamp.Pin_3_K1/A2
  GND: STM32.GND, INA219_-_MOTOR.gnd, INA219_-_Circuit.gnd, DS1.GND, Power_Supply.Pin_1, Motor_Driver_-_Cytron_MD10C.no_name_yet#connector_3, Motor_Driver_-_Cytron_MD10C.no_name_yet#connectornegative-2, Switch_Relay.GND, Power_distribution.0_-, Power_distribution.1_+, Power_distribution.7_+, Power_distribution.BAT-, J1.pin_2, COM.1, R2.Pin_0, C2.-, Negative_Clamp.Pin_1_A1
  N9: INA219_-_MOTOR.VIN-, Motor_Driver_-_Cytron_MD10C.no_name_yet#connectorpositive-1
  N10: INA219_-_MOTOR.VIN+, Motor_Fuse.Connector2
  N11: INA219_-_Circuit.VIN-, ExCircuit_+.1
  N12: INA219_-_Circuit.VIN+, J1.pin_3
  N13: Power_Supply.Pin_2, Main_Fuse.Connector1
  N14: Motor_Driver_-_Cytron_MD10C.no_name_yet#connectorA-3, 12V_DC_Motor.pin_2
  N15: Motor_Driver_-_Cytron_MD10C.no_name_yet#connectorB-4, 12V_DC_Motor.pin_1
  N16: Main_Fuse.Connector2, Kill_Switch.O
  N17: Kill_Switch.P, Power_distribution.BAT+
  N18: Switch_Relay.NO1, Motor_Fuse.Connector1
  N19: Switch_Relay.MAIN1, Power_distribution.1_-
  N20: Switch_Relay.NO2, Circuit_Fuse.Connector1
  N21: Switch_Relay.MAIN2, Power_distribution.2_-
  N22: Switch_Relay.VCC, Power_distribution.0_+
  N23: Circuit_Fuse.Connector2, J1.pin_1
  N24: J1.pin_4, ExCircuit_-.1
  N25: V-Probe.1, R1.Pin_1

notes:
  Raspberry Pi and STM32 are connected via USB

custom parts:
  INA219: INA219 current and voltage sensor breakout
  2RelayModule: 2 relay arduino module SONGLE SRD05VDC-SL-C
  PDP: Power Distibution Panel (PDP). Uses CAN to connect to roboRIO controller and provides 16 channels of power with current sensing at up to 30A or 40A (depending on port).
  XL4015 DC-DC CC CV module (blue): XL4015 DC-DC CC/CV module blue
  BAT54S Dual Schottky Clamp: BAT54S dual-series Schottky diode in SOT-23. Pin 1=A1, Pin 2=K2, Pin 3=K1/A2.
  Raspberry Pi 5: The RPi5, a faster version of the awesome Raspberry Pi4B ARM Board with 40 pin gpio.
